# Fritzing sketch carbulbflasher (saved by Fritzing 0.9.6b)
circuit board: 8.46667cm x 5.64444cm
breadboards: 1

parts:
  C1 = Ceramic Capacitor [capacitance=100nF voltage=35V package="100 mil [THT, multilayer]"]
  R1 = Resistor [tolerance=±5% power=0.25 resistance=68k package=THT]
  R2 = Resistor [tolerance=±5% power=0.25 resistance=220k package=THT]
  C2 = Ceramic Capacitor [capacitance=1pF voltage=35V package="100 mil [THT, multilayer]"]
  R3 = Resistor [tolerance=±5% power=0.25 resistance=22k package=THT]
  Q1 = PNP-Transistor [package="TO92 [THT]"]
  D1 = Rectifier Diode [part_number=1N4001 package="300 mil [THT]"]
  Q2 = Basic FET N-Channel [package="D2Pak [SMD]"]
  U1 = SWITCH-SPST-2 [package=r_sw_th]
  LED1 = LED - 5mm [color="Red (633nm)" current=0.030 package="5 mm [THT]"]
  VCC1 = Battery block 9V

nets:
  N1: C1.0, Q1.E, D1.cathode
  N2: C1.1, R1.Pin_0, R2.Pin_0, Q2.drain, U1.P, VCC1.-, VCC1.+
  N3: R1.Pin_1, R3.Pin_1, Q1.C, D1.anode, Q2.Gate, Q2.source, LED1.cathode
  N4: R2.Pin_1, C2.0, Q1.B
  N5: C2.1, R3.Pin_0
  N6: U1.O, LED1.anode
